# Fritzing sketch HVAC_Captive_Portal (saved by Fritzing 0.9.9b)
breadboards: 1

parts:
  Mod1 = Heltec WiFi LoRa 32 V2 [part_number=HTIT-WB32LA]
  Q1 = MOSFET-NCHANNEL [package=to-92]
  D1 = LTE-302 [package=lte-302]

nets:
  GND: Mod1.GND, Q1.S
  5V: Mod1.pin_20, D1.A
  N1: Mod1.pin_34, Q1.G
  N2: Q1.D, D1.C
